// Logisim project cpu.circ as structural Verilog: 3 circuits, main circuit main
module main (
  output [2:0] III,
  output X,
  output R,
  output [7:0] VVVV_VVVV
);

  wire R_t, X_t;
  wire [2:0] I, inst_to_aluc_1_out_2, rom_1_data;
  wire [7:0] PC_q, V;

  inst_to_aluc inst_to_aluc_1 (.in_1(I), .out_2(inst_to_aluc_1_out_2));
  Register R0 ();  // open: D, en, clk, Q, clr
  Register R1 ();  // open: D, en, clk, Q, clr
  Register PC (.Q(PC_q));  // open: D, en, clk, clr
  ROM #(.addrWidth(6), .dataWidth(16)) rom_1 (.addr(PC_q[6:1]), .data({V, R_t, X_t, I, rom_1_data}));
  RAM #(.addrWidth(7)) ram_1 ();  // open: addr, we, oe, clk, din, dout
  ALU alu_1 (.S(inst_to_aluc_1_out_2));  // open: A, B, out_4
endmodule

module ALU (
  input  [7:0] A,
  input  [7:0] B,
  input  [2:0] S,
  output [7:0] out_4
);

  wire [7:0] adder_1_out, and_1_out, multiplexer_1_out, not_1_out, or_1_out;

  assign not_1_out = ~B;  // NOT_Gate not_1, 8 bits wide
  Multiplexer #(.width(8)) multiplexer_1 (.in0(B), .in1(not_1_out), .out(multiplexer_1_out), .sel(S[2]));
  assign and_1_out = A & B;  // AND_Gate and_1, 8 bits wide
  assign or_1_out = A | B;  // OR_Gate or_1, 8 bits wide
  Adder adder_1 (.a(A), .b(multiplexer_1_out), .out(adder_1_out), .cin(S[2]));  // open: cout
  Multiplexer #(.select(2), .width(8)) multiplexer_2 (
    .in0(adder_1_out), .in1(and_1_out), .in2(or_1_out), .in3(A), .out(out_4), .sel(S[1:0]));
endmodule

module inst_to_aluc (
  input  [2:0] in_1,
  output [2:0] out_2
);

  wire and_1_out, and_2_out;

  and and_1 (and_1_out, ~in_1[0], in_1[1]);  // AND_Gate
  and and_2 (and_2_out, in_1[0], in_1[1]);
  and and_3 (out_2[2], in_1[0], ~in_1[1], in_1[2]);  // AND_Gate
  or or_1 (out_2[0], and_1_out, ~in_1[2]);  // OR_Gate
  or or_2 (out_2[1], and_2_out, ~in_1[2]);  // OR_Gate
endmodule
